# Fritzing sketch Sistema_Telemetria_PCB_FINAL (saved by Fritzing 0.9.9b)
circuit board: 14cm x 6.4cm
circuit board: 3.2cm x 5.4cm
circuit board: 3.8cm x 3cm
circuit board: 3.2cm x 5.4cm
circuit board: 3.8cm x 3cm
circuit board: 9.69936cm x 9.63678cm
breadboards: 1

parts:
  Mod1 = Heltec WiFi LoRa 32 V2 [part_number=HTIT-WB32LA]
  MPXV7002 = MPXV7002 Integrated Silicon Pressure Sensor
  MPU6050 = InvenSense MPU6050  # not connected
  BMP280 = BMP280 Breakout Board [part_number=BMP280]  # not connected
  Heltec_WiFi_LoRa_32_V2 = Heltec WiFi LoRa 32 V2 [part_number=HTIT-WB32LA]  # not connected
  J2 = female pin header, 18 pins [form="♀ (female)"]
  PITOT = Header 4 [package=jst-4-pth]
  MPU6050_2 = Header 4 [package=jst-4-pth]
  GPS = Header 4 [package=jst-4-pth]
  JP4 = Header 4 [package=jst-4-pth]
  JP5 = Header 4 [package=jst-4-pth]
  JP6 = Header 4 [package=jst-4-pth]
  JP7 = Header 4 [package=jst-4-pth]
  BMP = Header 4 [package=jst-4-pth]
  JP8 = Header 4 [package=jst-4-pth]
  JP9 = Header 4 [package=jst-4-pth]
  JP10 = Header 4 [package=jst-4-pth]
  JP11 = Header 4 [package=jst-4-pth]
  JP12 = Header 4 [package=jst-4-pth]
  JP13 = Header 4 [package=jst-4-pth]
  JP14 = Header 4 [package=jst-4-pth]
  J4 = male pin header, 3 pins [form="♂ (male)"]
  J5 = male pin header, 3 pins [form="♂ (male)"]
  J6 = male pin header, 3 pins [form="♂ (male)"]
  J7 = male pin header, 3 pins [form="♂ (male)"]
  J8 = male pin header, 3 pins [form="♂ (male)"]
  J9 = male pin header, 3 pins [form="♂ (male)"]
  J10 = male pin header, 3 pins [form="♂ (male)"]
  J11 = male pin header, 3 pins [form="♂ (male)"]
  J12 = male pin header, 3 pins [form="♂ (male)"]
  J13 = male pin header, 3 pins [form="♂ (male)"]
  J14 = male pin header, 3 pins [form="♂ (male)"]
  J15 = male pin header, 3 pins [form="♂ (male)"]
  J16 = male pin header, 3 pins [form="♂ (male)"]
  J18 = female pin header, 3 pins [form="♀ (female)"]
  J19 = female pin header, 3 pins [form="♀ (female)"]
  J20 = female pin header, 3 pins [form="♀ (female)"]
  J21 = female pin header, 3 pins [form="♀ (female)"]
  J22 = female pin header, 3 pins [form="♀ (female)"]
  J23 = female pin header, 3 pins [form="♀ (female)"]
  J24 = female pin header, 3 pins [form="♀ (female)"]
  J26 = female pin header, 2 pins [form="♀ (female)"]
  J27 = female pin header, 2 pins [form="♀ (female)"]
  J28 = female pin header, 2 pins [form="♀ (female)"]
  J29 = female pin header, 2 pins [form="♀ (female)"]
  J30 = female pin header, 2 pins [form="♀ (female)"]
  J31 = female pin header, 2 pins [form="♀ (female)"]
  SRV7 = Header 4 [package=jst-4-pth]
  SRV1 = Header 4 [package=jst-4-pth]
  SRV6 = Header 4 [package=jst-4-pth]
  SRV5 = Header 4 [package=jst-4-pth]
  SRV2 = Header 4 [package=jst-4-pth]
  SRV4 = Header 4 [package=jst-4-pth]
  SRV3 = Header 4 [package=jst-4-pth]
  J32 = male pin header, 3 pins [form="♂ (male)"]
  J33 = female pin header, 4 pins [form="♀ (female)"]
  GPS_2 = NEO-6M GPS Module [part_number=GY-GPS6MV2]
  J34 = female pin header, 3 pins [form="♀ (female)"]
  J35 = female pin header, 6 pins [form="♀ (female)"]
  J36 = female pin header, 8 pins [form="♀ (female)"]
  J25 = female pin header, 2 pins [form="♀ (female)"]
  Componente2 = ACS712 Current Sensor 5A 20A 30A  # not connected
  J3 = male pin header, 3 pins [form="♂ (male)"]
  Componente3 = ACS712 Current Sensor 5A 20A 30A  # not connected
  Componente4 = ACS712 Current Sensor 5A 20A 30A  # not connected
  Componente5 = ACS712 Current Sensor 5A 20A 30A  # not connected
  Componente6 = ACS712 Current Sensor 5A 20A 30A  # not connected
  Componente7 = ACS712 Current Sensor 5A 20A 30A  # not connected
  J1 = female pin header, 18 pins [form="♀ (female)"]
  Componente1 = ACS712 Current Sensor 5A 20A 30A  # not connected

nets:
  N1: Mod1.pin_12, MPXV7002.ANALOG
  N2: Mod1.pin_33, GPS_2.Tx
  N3: Mod1.pin_35, GPS_2.Rx
  N4: J2.pin2, SRV7.3
  N5: J2.pin3, SRV6.3
  N6: J2.pin8, SRV5.3
  N7: J2.pin9, SRV4.3
  N8: J2.pin12, PITOT.2
  N9: J2.pin13, SRV3.3
  N10: J2.pin14, SRV2.3
  N11: J2.pin15, SRV1.3
  N12: PITOT.3, MPU6050_2.4, GPS.4, BMP.3, SRV7.2, SRV1.2, SRV6.2, SRV5.2, SRV2.2, SRV4.2, SRV3.2, J32.pin1
  N13: PITOT.4, MPU6050_2.3, GPS.1, BMP.4, SRV7.4, SRV1.4, SRV6.4, SRV5.4, SRV2.4, SRV4.4, SRV3.4, J32.pin2
  N14: MPU6050_2.1, BMP.1, J1.pin3
  N15: MPU6050_2.2, BMP.2, J1.pin6
  N16: GPS.2, J1.pin2
  N17: GPS.3, J1.pin4
  N18: JP4.1, J33.pin1
  N19: JP4.2, J33.pin2
  N20: JP4.3, J33.pin3
  N21: JP4.4, J33.pin4
  N22: JP5.2, J34.pin1
  N23: JP5.3, J34.pin3
  N24: JP5.4, J34.pin2
  N25: JP6.1, J36.pin5
  N26: JP6.2, J36.pin6
  N27: JP6.3, J36.pin7
  N28: JP6.4, J36.pin8
  N29: JP7.1, J35.pin3
  N30: JP7.2, J35.pin4
  N31: JP7.3, J35.pin1, J35.pin2, J35.pin5
  N32: JP7.4, J35.pin6
  N33: JP8.1, J18.pin3
  N34: JP8.2, J18.pin2
  N35: JP8.3, J18.pin1
  N36: JP9.1, J19.pin3
  N37: JP9.2, J19.pin2
  N38: JP9.3, J19.pin1
  N39: JP10.1, J20.pin3
  N40: JP10.2, J20.pin2
  N41: JP10.3, J20.pin1
  N42: JP11.1, J21.pin3
  N43: JP11.2, J21.pin2
  N44: JP11.3, J21.pin1
  N45: JP12.1, J22.pin3
  N46: JP12.2, J22.pin2
  N47: JP12.3, J22.pin1
  N48: JP13.1, J23.pin3
  N49: JP13.2, J23.pin2
  N50: JP13.3, J23.pin1
  N51: JP14.1, J24.pin3
  N52: JP14.2, J24.pin2
  N53: JP14.3, J24.pin1
  N54: J4.pin1, J3.pin1
  N55: J4.pin2, J25.pin2
  N56: J4.pin3, J3.pin3
  N57: J5.pin1, J6.pin1
  N58: J5.pin2, J26.pin1
  N59: J5.pin3, J6.pin3
  N60: J6.pin2, J26.pin2
  N61: J7.pin1, J8.pin1
  N62: J7.pin2, J27.pin1
  N63: J7.pin3, J8.pin3
  N64: J8.pin2, J27.pin2
  N65: J9.pin1, J10.pin1
  N66: J9.pin2, J28.pin2
  N67: J9.pin3, J10.pin3
  N68: J10.pin2, J28.pin1
  N69: J11.pin1, J12.pin1
  N70: J11.pin2, J29.pin2
  N71: J11.pin3, J12.pin3
  N72: J12.pin2, J29.pin1
  N73: J13.pin1, J14.pin1
  N74: J13.pin2, J30.pin1
  N75: J13.pin3, J14.pin3
  N76: J14.pin2, J30.pin2
  N77: J15.pin1, J16.pin1
  N78: J15.pin2, J31.pin2
  N79: J15.pin3, J16.pin3
  N80: J16.pin2, J31.pin1
  N81: J25.pin1, J3.pin2

notes:
  MÓDULO LEITOR DE CORRENTE
  PITOT
  Vcc
  GND
  SCL
  SDA
  CSB
  TX
  RX
  VCC
  SINAL
  GPS
  SDO
  GIROSCOPIO
  BAROMETRO
  SRV1
  SRV2
  SRV3
  SRV4
  SRV5
  SRV6
  SRV7
  TELEMETRIA AERODESIGN V1.0
  XCL
  XDA
  INT
  ADO

custom parts:
  MPXV7002 Integrated Silicon Pressure Sensor: Description: The MPXV7002 piezoresistive transducer is a monolithic silicon pressure sensor manufactured by NXP Semiconductors. The transducer provides am analog output signal that is proportional to the applied pressure. Dimensions: 29mm x 21mm
  BMP280 Breakout Board: This is a breakout board for the Bosch Sensortec BMP280, "an absolute barometric pressure sensor especially designed for mobile applications." The operation range is 300 to 1100 hPa. Supply voltage is 1.2 to 3.6V. Operating temperature range is -40 to +85 °C.
  Heltec WiFi LoRa 32 V2: Heltec WiFi LoRa 32 V2 WiFi LoRa 32 is a classic IoT dev-board designed & produced by Heltec Automation(TM). It’s a highly integrated product based on ESP32 + SX127x, it has Wi-Fi, BLE, LoRa functions, also Li-Po battery management system, 0.96″ OLED are also included. It’s the best choice for smart cities, smart farms, smart home, and IoT makers.
  NEO-6M GPS Module: GY-GPS6MV2 NEO-6M GPS Module Module based on U-blox NEO-6M GPS engine, incorporating regulator for 3.3-5V DC input, MS621FE-compatible rechargeable battery for backup and EEPROM for storing configuration settings. Links: NEO-6 series product information page NEO-6 Datasheet
  ACS712 Current Sensor 5A 20A 30A: Remix by Michael Kubina http://www.kubina.info Original by: https://forum.fritzing.org/t/current-sensor-5a-acs712/7694 https://forum.fritzing.org/u/ArtHome ArtHome12@gmail.com
